# Fritzing sketch fan-speed-controller (saved by Fritzing 0.9.3b)
circuit board: 8.46667cm x 5.64444cm
breadboards: 1

parts:
  7805 = Voltage Regulator [package=to-220-alt]
  C1 = Ceramic Capacitor [capacitance=1µF package="100 mil [THT, multilayer]"]
  C2 = Ceramic Capacitor [capacitance=1µF package="100 mil [THT, multilayer]"]
  Q1 = Basic FET N-Channel [package="TO220 [THT]"]
  R1 = Resistor [tolerance=±5% resistance=220 package=THT]
  ATTINY45 = ATTINY45 [package=dip]
  M1 = DC Motor
  R2 = Resistor [tolerance=±5% resistance=10k package=THT]
  S1 = Round Pushbutton
  Q2 = NPN-Transistor [package="TO92 [THT]"]
  R3 = Resistor [tolerance=±5% resistance=10k package=THT]
  S2 = Round Pushbutton
  Q3 = NPN-Transistor [package="TO92 [THT]"]
  R4 = Resistor [tolerance=±5% resistance=10k package=THT]
  S3 = Round Pushbutton
  Q4 = NPN-Transistor [package="TO92 [THT]"]
  R5 = Resistor [tolerance=±5% resistance=10k package=THT]
  S4 = Round Pushbutton
  Q5 = NPN-Transistor [package="TO92 [THT]"]
  R6 = Resistor [tolerance=±5% resistance=10k package=THT]
  C3 = Ceramic Capacitor [capacitance=1µF package="100 mil [THT, multilayer]"]

nets:
  GND: 7805.GND, C1.0, C2.0, Q1.source, ATTINY45.GND, C3.0
  12V: 7805.IN, C2.1, M1.pin_1, S1.leg1, S2.leg1, S3.leg1, S4.leg1
  N1: 7805.OUT, C1.1, ATTINY45.VCC, R2.Pin_1, Q2.C, Q3.C, Q4.C, Q5.C
  N2: Q1.gate, R1.Pin_1, C3.1
  N3: Q1.drain, M1.pin_2
  N4: R1.Pin_0, ATTINY45.PB0(MOSI)
  N5: ATTINY45.PB5(NRES), R2.Pin_0
  N6: ATTINY45.PB3(ADC3), Q4.E
  N7: ATTINY45.PB4(ADC2), Q5.E
  N8: ATTINY45.PB1(MISO), Q2.E
  N9: ATTINY45.PB2(SCK_ADC1), Q3.E
  N10: S1.leg0, R3.Pin_1
  N11: Q2.B, R3.Pin_0
  N12: S2.leg0, R4.Pin_1
  N13: Q3.B, R4.Pin_0
  N14: S3.leg0, R5.Pin_1
  N15: Q4.B, R5.Pin_0
  N16: S4.leg0, R6.Pin_1
  N17: Q5.B, R6.Pin_0

notes:
  PWM
